# Fritzing sketch testbed (saved by Fritzing 1.0.6)
breadboards: 1

parts:
  Microcontroller = Arduino Mega 2560 (Rev3)
  PSU = Hanmatek HM305
  M1 = Stepper Motor - Bipolar
  R1 = Resistor [tolerance=±5% power=0.25W resistance=220k package=THT]
  R2 = Resistor [tolerance=±5% power=0.25W resistance=47k package=THT]
  C1 = Electrolytic Capacitor [capacitance=47µF voltage=50V package="200 mil [THT, electrolytic]"]
  Mod2 = TMC2209 [package=THT]

nets:
  N1: Microcontroller.A5, R1.Pin_1, R2.Pin_1
  N2: Microcontroller.D8_PWM, Mod2.EN
  N3: Microcontroller.5V, Mod2.VIO
  GND: Microcontroller.GND, PSU.Pin_3, R2.Pin_0, C1.-, Mod2.GND
  N4: Microcontroller.D2_PWM, Mod2.Step
  N5: Microcontroller.D5_PWM, Mod2.Dir
  N6: PSU.Pin_4, R1.Pin_0, C1.+, Mod2.VM
  N7: M1.A, Mod2.M1B
  N8: M1.C, Mod2.M1A
  N9: M1.B, Mod2.M2A
  N10: M1.D, Mod2.M2B

custom parts:
  Hanmatek HM305: DC Power Supply 30V5A HM305.
  TMC2209: TMC2209-LA stepper motor controller and driver. Supply voltage 4.75-28V Iphase up to 1.77A rms (2.5A peak)
